// Logisim project Part I 3).circ as structural Verilog: 1 circuit, main circuit main
module main (
);

  wire n7404_1_p3, n7408_1_p4, n7408_2_p2, n7432_1_p3, s_out, x_out, y_out;

  Button x (.out(x_out));
  Button y (.out(y_out));
  Button s (.out(s_out));
  // _7404 7404_1: pin names not known; wires that end beside it: s_out, s_out, n7404_1_p3, n7404_1_p3
  // _7408 7408_1: pin names not known; wires that end beside it: x_out, y_out, s_out, n7408_1_p4
  // _7408 7408_2: pin names not known; wires that end beside it: x_out, n7408_2_p2
  // _7432 7432_1: pin names not known; wires that end beside it: n7408_1_p4, n7408_2_p2, n7432_1_p3, n7432_1_p3
  LED led_1 (.in(n7432_1_p3));
endmodule
