// Logisim project Part II.circ as structural Verilog: 1 circuit, main circuit main
module main (
  input  a,
  input  b,
  input  c,
  input  d
);

  wire n7404_1_p2, n7404_2_p3, n7408_1_p2, n7408_2_p3, n7432_1_p3;

  // _7404 7404_1: pin names not known; wires that end beside it: c, n7404_1_p2, n7404_1_p2
  // _7404 7404_2: pin names not known; wires that end beside it: c, b, n7404_2_p3
  // _7408 7408_1: pin names not known; wires that end beside it: a, n7408_1_p2
  // _7408 7408_2: pin names not known; wires that end beside it: n7404_2_p3, d, n7408_2_p3
  // _7432 7432_1: pin names not known; wires that end beside it: n7408_1_p2, n7408_2_p3, n7432_1_p3
  LED led_1 (.in(n7432_1_p3));
endmodule
