// Logisim project part_i_chips.circ as structural Verilog: 1 circuit, main circuit main
module main (
  input  D
);

  wire n7400_1_p1, n7400_1_p4, n7400_1_p5, n7400_1_p7, n7404_1_p2;

  Clock clock_1 (.out(D));
  // _7404 7404_1: pin names not known; wires that end beside it: D, n7404_1_p2
  // _7400 7400_1: pin names not known; wires that end beside it: n7400_1_p1, D, n7404_1_p2, n7400_1_p4, n7400_1_p5, n7400_1_p4, n7400_1_p7, n7400_1_p1, n7400_1_p7, n7400_1_p5
  LED led_1 (.in(n7400_1_p7));
  LED led_2 (.in(n7400_1_p5));
endmodule
