// Logisim project part_i_gates.circ as structural Verilog: 1 circuit, main circuit main
module main (
  input  in_1
);

  wire clock_1_out, nand_1_out, nand_2_out, nand_3_out, nand_4_out, not_1_out;

  Clock clock_1 (.out(clock_1_out));
  nand nand_1 (nand_1_out, in_1, clock_1_out);
  nand nand_2 (nand_2_out, clock_1_out, not_1_out);
  not not_1 (not_1_out, in_1);
  nand nand_3 (nand_3_out, nand_1_out, nand_4_out);
  LED Qa (.in(nand_3_out));
  nand nand_4 (nand_4_out, nand_3_out, nand_2_out);
  LED Qb (.in(nand_4_out));
endmodule
